# Fritzing sketch lightbarrier (saved by Fritzing 0.9.3b)
breadboards: 1

parts:
  VCC1 = Battery
  Part1 = Arduino Uno (Rev3)
  R1 = Resistor [tolerance=±5% resistance=10k package=THT]
  R2 = Photocell (LDR) [package=THT]
  R3 = Resistor [tolerance=±5% resistance=220 package=THT]
  LED1 = LED - 5mm [color="Infrared (940nm)" package="5 mm [THT]"]  # not connected
  S1 = Pushbutton [package="[THT]"]
  R4 = Resistor [tolerance=±5% resistance=10k package=THT]
  LED2 = LED - 5mm [color="Red (633nm)" package="5 mm [THT]"]

nets:
  N1: VCC1.-, Part1.GND, R2.pin_1, R4.Pin_1, LED2.anode
  N2: VCC1.+, Part1.3V3, R1.Pin_1, R3.Pin_1, S1.Pin_3, S1.Pin_4
  N3: Part1.D12/MISO, LED2.cathode
  N4: Part1.D13/SCK, S1.Pin_1, S1.Pin_2, R4.Pin_0
  N5: Part1.D3_PWM, R1.Pin_0, R2.pin_0
